# Fritzing sketch Ldrled2 (saved by Fritzing 0.9.3b)
breadboards: 1

parts:
  U1 = NodeMCU V3.0
  R1 = Resistor [tolerance=±5% resistance=10k package=THT]
  R2 = Photocell (LDR) [package=THT]
  LED1 = LED - 5mm [color="Red (633nm)" package="5 mm [THT]"]

nets:
  N1: U1.3V3, R2.pin_0
  N2: U1.GND#6, U1.GND#13, U1.GND#16, U1.GND#33
  N3: U1.D8, LED1.anode
  N4: U1.GND#41, LED1.cathode
  N5: U1.A0, R1.Pin_0, R2.pin_1

custom parts:
  NodeMCU V3.0: ESP8266 based NodeMCU

// code stored in the sketch: codLRD_led.ino

int lightPin = 0;// A0 pin anal?gico de entrada para el LDR
int led= 15; //D1 donde se conecta el led
int valorLDR=0;

void setup() 
{
    Serial.begin(9600);
}

void loop() 
{
  //apagar el led siempre que inicia el ciclo
  //digitalWrite(led, LOW);
  valorLDR= analogRead(lightPin); //valor anal?gico , mas alto 1024
  int reading  = 1024- valorLDR; //1023*4 //Variable que almacena el valor del LDR
  
 analogWrite(led ,reading);
  //Serial.println(valorLDR);
  delay(1000);
  Serial.println(reading);
   

 
}
